# Fritzing sketch DoorSign (saved by Fritzing 0.9.4)
circuit board: 8.46667cm x 5.64444cm

parts:
  LCD1 = LCD screen
  LVL1 = Logic Level Converter
  LED1 = LED - 5mm [color="Red (633nm)" package="5 mm [THT]"]
  R1 = Trimmer Potentiometer [maximum_resistance=10kΩ package=THT]
  Q1 = NPN-Transistor [package="TO92 [THT]"]
  LVL2 = Logic Level Converter
  WeMos_D1_Mini1 = WeMos D1 Mini
  J1 = double row female pin header, 16 pins [form="♀ (female)"]

nets:
  VSS: LCD1.VSS, LCD1.R/W, LVL1.GND, LED1.cathode, R1.leg1, Q1.C, WeMos_D1_Mini1.G, J1.pin1, J1.pin5
  VDD: LCD1.VDD, LCD1.LED+, LVL1.HV, R1.leg2, LVL2.HV, WeMos_D1_Mini1.5V, J1.pin2, J1.pin15
  N1: LCD1.V0, R1.wiper, J1.pin3
  N2: LCD1.RS, LVL2.RX_HV, J1.pin4
  N3: LCD1.E, LVL2.TX_HV, J1.pin6
  N4: LCD1.DB0, J1.pin7
  N5: LCD1.DB4, LVL1.TX2_HV, J1.pin11
  N6: LCD1.DB5, LVL1.RX2_HV, J1.pin12
  N7: LCD1.DB6, LVL1.RX_HV, J1.pin13
  N8: LCD1.DB7, LVL1.TX_HV, J1.pin14
  N9: LCD1.LED-, Q1.E, J1.pin16
  N10: LVL1.TX2_LV, WeMos_D1_Mini1.D5
  N11: LVL1.RX2_LV, WeMos_D1_Mini1.D6
  N12: LVL1.LV, LVL2.LV, WeMos_D1_Mini1.3V3
  N13: LVL1.RX_LV, WeMos_D1_Mini1.D7
  N14: LVL1.TX_LV, WeMos_D1_Mini1.D8
  N15: LED1.anode, WeMos_D1_Mini1.D4
  N16: Q1.B, LVL2.TX2_HV
  N17: LVL2.TX2_LV, WeMos_D1_Mini1.D3
  N18: LVL2.RX_LV, WeMos_D1_Mini1.D2
  N19: LVL2.TX_LV, WeMos_D1_Mini1.D1
